// Digital circuit somador_vetorial_FINAL.dig as structural Verilog
module somador_vetorial_FINAL (
  input  [31:0] Vetor_A,
  input  [31:0] Vetor_B,
  input  [1:0] \Número_de_Bits ,
  input  in_4
);

  wire [31:0] u_SomadorVetorial_s_o;

  SomadorVetorial #(.applicationType("GHDL"), .CodeFile("C:\\Users\\jvcha\\SD_pratica\\somador_vetorial_A.vhdl")) u_SomadorVetorial (
    .A_i(Vetor_A), .B_i(Vetor_B), .vecSize_i(\Número_de_Bits ), .mode_i(in_4), .S_o(u_SomadorVetorial_s_o));
  // Probe Output on u_SomadorVetorial_s_o
endmodule
